# Fritzing sketch WiringGuide (saved by Fritzing 0.9.3b)
breadboards: 1

parts:
  Part1 = Arduino Leonardo (Rev3b)
  Part2 = Arduino GPS Shield

nets:
  N1: Part1.D3_PWM/SCL, Part2.D_TX
  N2: Part1.D11_PWM, Part2.D_RX

notes:
  [No representation of the M6E Nano so using GPS to show cable connections
